// Logisim project ALU4.circ as structural Verilog: 4 circuits, main circuit main
module main (
  input  [3:0] A,
  input  [3:0] B,
  input  Control1,
  input  Control2,
  output [3:0] Result,
  output Zero,
  output Negative,
  output Overflow,
  output Carry
);

  wire or_2_out;
  wire [3:0] AND_result, multiplexer_1_out, n4_bit_adder_subtractor_result, OR_result;

  _4_Bit_AND AND (.A(A), .B(B), .Result(AND_result));
  _4_Bit_OR OR (.A(A), .B(B), .Result(OR_result));
  _4_Bit_Adder_Subtractor u_4_bit_adder_subtractor (
    .Add_Sub_Control(Control1), .A(A), .B(B), .Result(n4_bit_adder_subtractor_result), .Carry_Out(Overflow),
    .Overflow(Carry));
  Multiplexer #(.width(4), .enable("false")) multiplexer_1 (
    .in0(AND_result), .in1(OR_result), .out(multiplexer_1_out), .sel(Control1));
  Multiplexer #(.width(4), .enable("false")) multiplexer_2 (
    .in0(multiplexer_1_out), .in1(n4_bit_adder_subtractor_result), .out({Negative, Result[2:0]}),
    .sel(Control2));
  or or_2 (or_2_out, Result[0], Result[1], Result[2], Negative);
  not not_1 (Zero, or_2_out);

  assign Result[3] = Negative;
endmodule

module _4_Bit_AND (
  input  [3:0] A,
  input  [3:0] B,
  output [3:0] Result
);

  and and_1 (Result[0], A[0], B[0]);
  and and_2 (Result[1], A[1], B[1]);
  and and_3 (Result[2], A[2], B[2]);
  and and_4 (Result[3], A[3], B[3]);
endmodule

module _4_Bit_OR (
  input  [3:0] A,
  input  [3:0] B,
  output [3:0] Result
);

  or or_1 (Result[0], A[0], B[0]);
  or or_2 (Result[1], A[1], B[1]);
  or or_3 (Result[2], A[2], B[2]);
  or or_4 (Result[3], A[3], B[3]);
endmodule

module _4_Bit_Adder_Subtractor (
  input  Add_Sub_Control,
  input  [3:0] A,
  input  [3:0] B,
  output [3:0] Result,
  output Carry_Out,
  output Overflow
);

  wire adder_1_cout, adder_2_cout, adder_3_cout, and_1_out, and_2_out, not_1_out, not_2_out, not_3_out,
       xor_1_out, xor_2_out, xor_3_out, xor_4_out;

  xor xor_1 (xor_1_out, Add_Sub_Control, B[0]);
  xor xor_2 (xor_2_out, Add_Sub_Control, B[1]);
  xor xor_3 (xor_3_out, Add_Sub_Control, B[2]);
  xor xor_4 (xor_4_out, Add_Sub_Control, B[3]);
  not not_1 (not_1_out, xor_4_out);
  not not_2 (not_2_out, A[3]);
  Adder #(.width(1)) adder_1 (.a(A[0]), .b(xor_1_out), .out(Result[0]), .cin(Add_Sub_Control), .cout(adder_1_cout));
  Adder #(.width(1)) adder_2 (.a(A[1]), .b(xor_2_out), .out(Result[1]), .cin(adder_1_cout), .cout(adder_2_cout));
  Adder #(.width(1)) adder_3 (.a(A[2]), .b(xor_3_out), .out(Result[2]), .cin(adder_2_cout), .cout(adder_3_cout));
  Adder #(.width(1)) adder_4 (.a(A[3]), .b(xor_4_out), .out(Result[3]), .cin(adder_3_cout), .cout(Carry_Out));
  not not_3 (not_3_out, Result[3]);
  and and_1 (and_1_out, not_2_out, not_1_out, Result[3]);
  and and_2 (and_2_out, not_3_out, A[3], xor_4_out);
  or or_1 (Overflow, and_1_out, and_2_out);
endmodule
