// Logisim project ALU8.circ as structural Verilog: 4 circuits, main circuit main
module main (
  input  [7:0] A,
  input  [7:0] B,
  input  Control1,
  input  Control2,
  output [7:0] Result,
  output Zero,
  output Negative,
  output Overflow,
  output Carry
);

  wire or_2_out;
  wire [7:0] ADD_SUB_result, AND_result, multiplexer_1_out, OR_result;

  _4_Bit_AND AND (.A(A), .B(B), .Result(AND_result));
  _4_Bit_OR OR (.A(A), .B(B), .Result(OR_result));
  _4_Bit_Adder_Subtractor ADD_SUB (
    .Add_Sub_Control(Control1), .A(A), .B(B), .Result(ADD_SUB_result), .Carry_Out(Overflow), .Overflow(Carry));
  Multiplexer #(.width(8), .enable("false")) multiplexer_1 (
    .in0(AND_result), .in1(OR_result), .out(multiplexer_1_out), .sel(Control1));
  Multiplexer #(.width(8), .enable("false")) multiplexer_2 (
    .in0(multiplexer_1_out), .in1(ADD_SUB_result), .out({Negative, Result[6:0]}), .sel(Control2));
  not not_1 (Zero, or_2_out);
  or or_2 (or_2_out, Result[0], Result[1], Result[2], Result[3], Result[4], Result[5], Result[6], Negative);

  assign Result[7] = Negative;
endmodule

module _4_Bit_AND (
  input  [7:0] A,
  input  [7:0] B,
  output [7:0] Result
);

  assign Result = A & B;  // AND_Gate and_1, 8 bits wide
endmodule

module _4_Bit_OR (
  input  [7:0] A,
  input  [7:0] B,
  output [7:0] Result
);

  assign Result = A | B;  // OR_Gate or_1, 8 bits wide
endmodule

module _4_Bit_Adder_Subtractor (
  input  Add_Sub_Control,
  input  [7:0] A,
  input  [7:0] B,
  output [7:0] Result,
  output Carry_Out,
  output Overflow
);

  wire adder_1_cout, adder_2_cout, adder_3_cout, adder_4_cout, adder_5_cout, adder_6_cout, adder_7_cout,
       and_1_out, and_2_out, not_1_out, not_2_out, not_3_out, xor_1_out, xor_2_out, xor_3_out, xor_4_out,
       xor_5_out, xor_6_out, xor_7_out, xor_8_out;

  xor xor_1 (xor_1_out, Add_Sub_Control, B[0]);
  xor xor_2 (xor_2_out, Add_Sub_Control, B[1]);
  xor xor_3 (xor_3_out, Add_Sub_Control, B[2]);
  xor xor_4 (xor_4_out, Add_Sub_Control, B[3]);
  xor xor_5 (xor_5_out, Add_Sub_Control, B[4]);
  xor xor_6 (xor_6_out, Add_Sub_Control, B[5]);
  xor xor_7 (xor_7_out, Add_Sub_Control, B[6]);
  xor xor_8 (xor_8_out, Add_Sub_Control, B[7]);
  not not_1 (not_1_out, xor_8_out);
  not not_2 (not_2_out, A[7]);
  Adder #(.width(1)) adder_1 (.a(A[0]), .b(xor_1_out), .out(Result[0]), .cin(Add_Sub_Control), .cout(adder_1_cout));
  Adder #(.width(1)) adder_2 (.a(A[1]), .b(xor_2_out), .out(Result[1]), .cin(adder_1_cout), .cout(adder_2_cout));
  Adder #(.width(1)) adder_3 (.a(A[2]), .b(xor_3_out), .out(Result[2]), .cin(adder_2_cout), .cout(adder_3_cout));
  Adder #(.width(1)) adder_4 (.a(A[3]), .b(xor_4_out), .out(Result[3]), .cin(adder_3_cout), .cout(adder_4_cout));
  Adder #(.width(1)) adder_5 (.a(A[4]), .b(xor_5_out), .out(Result[4]), .cin(adder_4_cout), .cout(adder_5_cout));
  Adder #(.width(1)) adder_6 (.a(A[5]), .b(xor_6_out), .out(Result[5]), .cin(adder_5_cout), .cout(adder_6_cout));
  Adder #(.width(1)) adder_7 (.a(A[6]), .b(xor_7_out), .out(Result[6]), .cin(adder_6_cout), .cout(adder_7_cout));
  Adder #(.width(1)) adder_8 (.a(A[7]), .b(xor_8_out), .out(Result[7]), .cin(adder_7_cout), .cout(Carry_Out));
  not not_3 (not_3_out, Result[7]);
  and and_1 (and_1_out, not_2_out, not_1_out, Result[7]);
  and and_2 (and_2_out, not_3_out, A[7], xor_8_out);
  or or_1 (Overflow, and_1_out, and_2_out);
endmodule
