// Logisim project datapath.circ as structural Verilog: 3 circuits, main circuit Datapath
module Datapath (
  input  Reset,
  input  Clear,
  input  Clear_2
);

  wire alu_1_p4, and_2_out, and_3_out, Clock_out, control_1_alusrc, control_1_branch, control_1_memread,
       control_1_memtoreg, control_1_memwrite, control_1_regdst, control_1_regwrite, instructiondecode_1_p3,
       instructiondecode_1_p7, not_1_out, registers_1_p5, registers_1_p7;
  wire [1:0] control_1_aluop;
  wire [3:0] alu_1_p3;
  wire [4:0] instructiondecode_1_p4, instructiondecode_1_p5, multiplexer_1_out;
  wire [5:0] instructiondecode_1_p2, instructiondecode_1_p6;
  wire [7:0] wordaddress_1_p2, wordaddress_2_p2;
  wire [31:0] adder_1_out, alu_1_p2, branchaddress_1_p3, memorydata_1_p2, memorydata_1_p5, multiplexer_3_out,
       ram_1_data, registers_1_p4, registers_1_p8, signextend_1_p2, wordaddress_1_p1, wordaddress_2_p1;

  // WordAddress wordaddress_1: pin names not known; wires that end beside it: wordaddress_1_p1, wordaddress_1_p2
  Clock Clock (.out(Clock_out));
  Register #(.width(32)) register_1 (
    .D(multiplexer_3_out), .Q(wordaddress_1_p1), .clk(Clock_out), .clr(Reset));  // open: en
  RAM #(.dataWidth(32)) ram_1 (
    .addr(wordaddress_1_p2), .data(ram_1_data), .sel(1'b1), .clk(1'b0), .ld(1'b1), .clr(Clear));
  Control control_1 (
    .op(instructiondecode_1_p2), .RegDst(control_1_regdst), .Branch(control_1_branch),
    .MemRead(control_1_memread), .MemToReg(control_1_memtoreg), .ALUop(control_1_aluop),
    .MemWrite(control_1_memwrite), .ALUsrc(control_1_alusrc), .RegWrite(control_1_regwrite));  // open: test
  // InstructionDecode instructiondecode_1: pin names not known; wires that end beside it: ram_1_data, instructiondecode_1_p2, instructiondecode_1_p3, instructiondecode_1_p4, instructiondecode_1_p5, instructiondecode_1_p6, instructiondecode_1_p7
  Multiplexer #(.width(5), .enable("false")) multiplexer_1 (
    .in0(instructiondecode_1_p4), .in1(instructiondecode_1_p5), .out(multiplexer_1_out),
    .sel(control_1_regdst));
  not not_1 (not_1_out, Clock_out);
  Adder #(.width(32)) adder_1 (.a(32'h4), .b(wordaddress_1_p1), .out(adder_1_out));  // open: cin, cout
  // Registers registers_1: pin names not known; wires that end beside it: instructiondecode_1_p3, instructiondecode_1_p4, multiplexer_1_out, registers_1_p4, registers_1_p5, Reset, registers_1_p7, registers_1_p8
  // SignExtend signextend_1: pin names not known; wires that end beside it: instructiondecode_1_p7, signextend_1_p2
  and and_1 (registers_1_p5, control_1_regwrite, not_1_out);
  // WordAddress wordaddress_2: pin names not known; wires that end beside it: wordaddress_2_p1, wordaddress_2_p2
  // BranchAddress branchaddress_1: pin names not known; wires that end beside it: adder_1_out, signextend_1_p2, branchaddress_1_p3
  // ALU alu_1: pin names not known; wires that end beside it: registers_1_p7, alu_1_p2, alu_1_p3, alu_1_p4, wordaddress_2_p1
  Multiplexer #(.width(32), .enable("false")) multiplexer_2 (
    .in0(registers_1_p8), .in1(signextend_1_p2), .out(alu_1_p2), .sel(control_1_alusrc));
  ALUcontrol alucontrol_1 (
    .funct(instructiondecode_1_p6), .ALUop(control_1_aluop), .Operation(alu_1_p3));  // open: test
  and and_2 (and_2_out, not_1_out, control_1_memwrite);
  Multiplexer #(.width(32), .enable("false")) multiplexer_3 (
    .in0(adder_1_out), .in1(branchaddress_1_p3), .out(multiplexer_3_out), .sel(and_3_out));
  and and_3 (and_3_out, control_1_branch, alu_1_p4);
  Multiplexer #(.width(32), .enable("false")) multiplexer_4 (
    .in0(wordaddress_2_p1), .in1(memorydata_1_p5), .out(registers_1_p4), .sel(control_1_memtoreg));
  // MemoryData memorydata_1: pin names not known; wires that end beside it: registers_1_p8, memorydata_1_p2, control_1_memwrite, control_1_memread, memorydata_1_p5, memorydata_1_p2
  RAM #(.dataWidth(32)) ram_2 (
    .addr(wordaddress_2_p2), .data(memorydata_1_p2), .sel(1'b1), .clk(and_2_out), .ld(control_1_memread),
    .clr(Clear_2));

  // Notes on the sheet:
  //   Toby Chappell
  //   12/4/19
  //   Instruction Memory
  //   Decode
  //   PC
  //   Control
  //   Registers
  //   Extend
  //   Branch
  //   ALU
  //   ALU control
  //   Data Memory
endmodule

module Control (
  input  [8:0] test,
  input  [5:0] op,
  output RegDst,
  output Branch,
  output MemRead,
  output MemToReg,
  output [1:0] ALUop,
  output MemWrite,
  output ALUsrc,
  output RegWrite
);


  assign ALUop = {test[3], test[4]};
  assign ALUsrc = test[1];
  assign Branch = test[7];
  assign MemRead = test[6];
  assign MemToReg = test[5];
  assign MemWrite = test[2];
  assign RegDst = test[8];
  assign RegWrite = test[0];
endmodule

module ALUcontrol (
  input  [3:0] test,
  input  [5:0] funct,
  input  [1:0] ALUop,
  output [3:0] Operation
);


  assign Operation = test;
endmodule
