// Logisim project 4-bit Adder.circ as structural Verilog: 1 circuit, main circuit main
module main (
  input  A0,
  input  B0,
  input  A1,
  input  B1,
  input  A2,
  input  B2,
  input  A3,
  input  B3,
  input  [3:0] A3_2,
  input  [3:0] B3_2,
  output S0,
  output S1,
  output S2,
  output S3,
  output C_out,
  output [3:0] S3_2,
  output out_17
);

  wire adder_1_cout, adder_2_cout, adder_3_cout;

  Adder #(.width(1)) adder_1 (.a(A0), .b(B0), .out(S0), .cout(adder_1_cout));  // open: cin
  Adder #(.width(1)) adder_2 (.a(A1), .b(B1), .out(S1), .cin(adder_1_cout), .cout(adder_2_cout));
  Adder #(.width(1)) adder_3 (.a(A2), .b(B2), .out(S2), .cin(adder_2_cout), .cout(adder_3_cout));
  Adder #(.width(1)) adder_4 (.a(A3), .b(B3), .out(S3), .cin(adder_3_cout), .cout(C_out));
  Adder #(.width(4)) adder_5 (.a(A3_2), .b(B3_2), .out(S3_2), .cout(out_17));  // open: cin
endmodule
