// Logisim project Flip-Flop.circ as structural Verilog
module D_Flip_Flop (
  input  D,
  output Q,
  output Q_prime,
  output Q_2,
  output Q_prime_2
);

  wire clock_1_out, nand_1_out, nand_2_out, not_1_out;

  Clock clock_1 (.out(clock_1_out));
  not not_1 (not_1_out, D);
  D_Flip_Flop_part d_ff_1 (.clk(clock_1_out), .D(D), .Q(Q_2), .Qn(Q_prime_2));  // open: preset, en, reset
  nand nand_1 (nand_1_out, D, clock_1_out);
  nand nand_2 (nand_2_out, clock_1_out, not_1_out);
  nand nand_3 (Q, nand_1_out, Q_prime);
  nand nand_4 (Q_prime, Q, nand_2_out);
endmodule

module SR_Flip_Flop (
  input  S,
  input  R,
  output Q,
  output Q_prime,
  output Q_2,
  output Q_prime_2
);

  wire clock_1_out, nand_1_out, nand_2_out;

  Clock clock_1 (.out(clock_1_out));
  S_R_Flip_Flop s_r_ff_1 (.S(S), .clk(clock_1_out), .R(R), .Q(Q_2), .Qn(Q_prime_2));  // open: preset, reset, en
  nand nand_1 (nand_1_out, S, clock_1_out);
  nand nand_2 (nand_2_out, clock_1_out, R);
  nand nand_3 (Q, nand_1_out, Q_prime);
  nand nand_4 (Q_prime, Q, nand_2_out);
endmodule
