// Logisim project Full-Adder 2.circ as structural Verilog: 1 circuit, main circuit main
module main (
  input  C_in,
  input  A,
  input  B,
  output S,
  output C_out
);

  Adder #(.width(1)) adder_1 (.a(A), .b(B), .out(S), .cin(C_in), .cout(C_out));
endmodule
