// Logisim project Magnitude Comparator.circ as structural Verilog: 1 circuit, main circuit main
module main (
  input  A0,
  input  B0,
  input  A1,
  input  B1,
  input  A2,
  input  B2,
  input  A3,
  input  B3,
  input  [3:0] A,
  input  [3:0] B,
  output A_EQ_B,
  output A_EQ_B_2
);

  wire and_1_out, and_2_out, xnor_1_out, xnor_2_out, xnor_3_out, xnor_4_out;

  xnor xnor_1 (xnor_1_out, A0, B0);
  xnor xnor_2 (xnor_2_out, A1, B1);
  xnor xnor_3 (xnor_3_out, A2, B2);
  xnor xnor_4 (xnor_4_out, A3, B3);
  Comparator #(.width(4)) comparator_1 (.a(A), .b(B), .eq(A_EQ_B_2));  // open: gt, lt
  and and_1 (and_1_out, xnor_1_out, xnor_2_out);
  and and_2 (and_2_out, xnor_3_out, xnor_4_out);
  and and_3 (A_EQ_B, and_1_out, and_2_out);
endmodule
